// Logisim project lab7_part1 (1).circ as structural Verilog: 1 circuit, main circuit main
module main (
  input  in_1,
  input  in_2,
  input  in_3,
  input  in_4,
  input  in_5,
  input  in_6,
  input  in_7,
  input  in_8,
  input  in_9,
  input  in_10
);

  wire and_1_out, multiplexer_1_out, multiplexer_2_out, not_1_out, not_2_out, not_3_out, not_4_out;
  wire [3:0] counter_2_q, ram_1_dout;
  wire [4:0] counter_1_q;

  Counter #(.max('h1f), .width(5)) counter_1 (
    .clr(in_3), .load(in_4), .up(in_5), .count(in_6), .clk(in_6), .Q(counter_1_q));  // open: D, carry
  Multiplexer #(.enable("false")) multiplexer_1 (.in0(in_7), .in1(1'b1), .out(multiplexer_1_out), .sel(and_1_out));
  Counter #(.max('hf), .width(4)) counter_2 (
    .clr(in_8), .load(multiplexer_1_out), .up(in_9), .clk(in_6), .D(4'b0001), .Q(counter_2_q));  // open: count, carry
  RAM #(.addrWidth(5), .dataWidth(4)) ram_1 (
    .addr(counter_1_q), .we(in_2), .oe(in_1), .clk(in_6), .din(counter_2_q), .dout(ram_1_dout));
  not not_1 (not_1_out, counter_1_q[0]);
  not not_2 (not_2_out, counter_1_q[1]);
  not not_3 (not_3_out, counter_1_q[2]);
  not not_4 (not_4_out, counter_1_q[3]);
  Multiplexer #(.enable("false")) multiplexer_2 (.in0(and_1_out), .in1(1'b1), .out(multiplexer_2_out), .sel(in_10));
  and and_1 (and_1_out, not_1_out, not_2_out, not_3_out, not_4_out, counter_1_q[4]);
  Hex_Digit_Display hex_digit_display_1 (.value(ram_1_dout));  // open: dp
endmodule
