// Logisim project lab7_part2 (2).circ as structural Verilog: 5 circuits, main circuit main
module main (
  input  in_1,
  input  in_2,
  input  in_3,
  input  in_4,
  input  in_5,
  input  in_6,
  input  in_7,
  input  in_8,
  input  in_9,
  input  in_10
);

  wire and_1_out, and_2_out, multiplexer_1_out, multiplexer_2_out, not_1_out, not_2_out, not_3_out, not_4_out;
  wire [3:0] counter_2_q, ram_1_dout;
  wire [4:0] counter_1_q;

  Counter #(.max('h1f), .width(5)) counter_1 (
    .clr(in_3), .load(in_4), .up(in_5), .count(in_6), .clk(in_6), .Q(counter_1_q));  // open: D, carry
  Multiplexer #(.enable("false")) multiplexer_1 (.in0(in_7), .in1(1'b1), .out(multiplexer_1_out), .sel(and_2_out));
  Counter #(.max('hf), .width(4)) counter_2 (
    .clr(in_8), .load(multiplexer_1_out), .up(in_9), .clk(in_6), .D(4'b0001), .Q(counter_2_q));  // open: count, carry
  RAM #(.addrWidth(5), .dataWidth(4)) ram_1 (
    .addr(counter_1_q), .we(in_2), .oe(in_1), .clk(in_6), .din(counter_2_q), .dout(ram_1_dout));
  not not_1 (not_1_out, counter_1_q[0]);
  not not_2 (not_2_out, counter_1_q[1]);
  not not_3 (not_3_out, counter_1_q[2]);
  not not_4 (not_4_out, counter_1_q[3]);
  Multiplexer #(.enable("false")) multiplexer_2 (.in0(and_2_out), .in1(1'b1), .out(multiplexer_2_out), .sel(in_10));
  and and_1 (and_1_out, counter_1_q[0], not_2_out, not_3_out, not_4_out, counter_1_q[4]);
  and and_2 (and_2_out, not_1_out, not_2_out, not_3_out, not_4_out, counter_1_q[4]);
  Hex_Digit_Display hex_digit_display_1 (.value(ram_1_dout));  // open: dp
endmodule

module Lab7Part2 (
  input  [23:0] in_1,
  input  En,
  input  Reset,
  input  [6:0] X,
  input  [6:0] Y
);

  wire clock_1_out;
  wire [6:0] rgb_video_1_p5, rgb_video_1_p6;

  Clock clock_1 (.out(clock_1_out));
  // RGB_Video rgb_video_1: pin names not known; wires that end beside it: clock_1_out, Reset, clock_1_out, En, rgb_video_1_p5, rgb_video_1_p6, in_1
  FSM_Part2 fsm_part2_1 (.Clk(clock_1_out), .x(X), .Reset(Reset), .y(Y), .XOut(rgb_video_1_p5), .YOut(rgb_video_1_p6));
endmodule

module FSM_Part2 (
  input  Clk,
  input  [6:0] x,
  input  Reset,
  input  [6:0] y,
  output [6:0] XOut,
  output [6:0] YOut
);

  wire nor_1_out, nor_2_out, undriven;
  wire [3:0] counter_2_q, counter_4_q;

  Counter #(.max('h7f), .width(7)) counter_1 (
    .load(nor_1_out), .up(1'b1), .clk(Clk), .D(x), .Q(XOut));  // open: clr, count, carry
  Counter #(.max('hf), .width(4)) counter_2 (
    .clr(Reset), .load(1'b0), .up(1'b1), .clk(Clk), .Q(counter_2_q));  // open: count, D, carry
  Counter #(.max('h7f), .width(7)) counter_3 (
    .clr(undriven), .load(nor_2_out), .up(1'b1), .clk(nor_1_out), .D(y), .Q(YOut));  // open: count, carry
  Counter #(.max('hf), .width(4)) counter_4 (
    .clr(Reset), .load(1'b0), .up(1'b1), .clk(nor_1_out), .Q(counter_4_q));  // open: count, D, carry
  nor nor_1 (nor_1_out, counter_2_q[0], counter_2_q[1], counter_2_q[2], counter_2_q[3]);
  nor nor_2 (nor_2_out, counter_4_q[0], counter_4_q[1], counter_4_q[2], counter_4_q[3]);
endmodule

module Part1 (
  input  in_1,
  input  in_2,
  input  in_3,
  input  in_4,
  input  in_5,
  input  in_6,
  input  in_7,
  input  in_8,
  input  in_9,
  input  in_10
);

  wire and_1_out, and_2_out, multiplexer_1_out, multiplexer_2_out, not_1_out, not_2_out, not_3_out, not_4_out;
  wire [3:0] counter_2_q, ram_1_dout;
  wire [4:0] counter_1_q;

  Counter #(.max('h1f), .width(5)) counter_1 (
    .clr(in_3), .load(in_4), .up(in_5), .count(in_6), .clk(in_6), .Q(counter_1_q));  // open: D, carry
  Multiplexer #(.enable("false")) multiplexer_1 (.in0(in_7), .in1(1'b1), .out(multiplexer_1_out), .sel(and_2_out));
  Counter #(.max('hf), .width(4)) counter_2 (
    .clr(in_8), .load(multiplexer_1_out), .up(in_9), .clk(in_6), .D(4'b0001), .Q(counter_2_q));  // open: count, carry
  RAM #(.addrWidth(5), .dataWidth(4)) ram_1 (
    .addr(counter_1_q), .we(in_2), .oe(in_1), .clk(in_6), .din(counter_2_q), .dout(ram_1_dout));
  not not_1 (not_1_out, counter_1_q[0]);
  not not_2 (not_2_out, counter_1_q[1]);
  not not_3 (not_3_out, counter_1_q[2]);
  not not_4 (not_4_out, counter_1_q[3]);
  Multiplexer #(.enable("false")) multiplexer_2 (.in0(and_2_out), .in1(1'b1), .out(multiplexer_2_out), .sel(in_10));
  and and_1 (and_1_out, counter_1_q[0], not_2_out, not_3_out, not_4_out, counter_1_q[4]);
  and and_2 (and_2_out, not_1_out, not_2_out, not_3_out, not_4_out, counter_1_q[4]);
  Hex_Digit_Display hex_digit_display_1 (.value(ram_1_dout));  // open: dp
endmodule

module DataPathControlUnit (
  input  Clk,
  input  [6:0] x,
  input  Reset,
  input  [6:0] y,
  output [6:0] XOut,
  output [6:0] YOut
);

  wire nor_1_out, nor_2_out, undriven;
  wire [3:0] counter_2_q, counter_4_q;

  Counter #(.max('h7f), .width(7)) counter_1 (
    .load(nor_1_out), .up(1'b1), .clk(Clk), .D(x), .Q(XOut));  // open: clr, count, carry
  Counter #(.max('hf), .width(4)) counter_2 (
    .clr(Reset), .load(1'b0), .up(1'b1), .clk(Clk), .Q(counter_2_q));  // open: count, D, carry
  Counter #(.max('h7f), .width(7)) counter_3 (
    .clr(undriven), .load(nor_2_out), .up(1'b1), .clk(nor_1_out), .D(y), .Q(YOut));  // open: count, carry
  Counter #(.max('hf), .width(4)) counter_4 (
    .clr(Reset), .load(1'b0), .up(1'b1), .clk(nor_1_out), .Q(counter_4_q));  // open: count, D, carry
  nor nor_1 (nor_1_out, counter_2_q[0], counter_2_q[1], counter_2_q[2], counter_2_q[3]);
  nor nor_2 (nor_2_out, counter_4_q[0], counter_4_q[1], counter_4_q[2], counter_4_q[3]);
endmodule
