// Logisim project lab2_part1.circ as structural Verilog: 3 circuits, main circuit main
module main (
  input  Input1,
  input  Input2,
  input  Input3,
  input  Input4,
  input  S1,
  input  S2,
  output O
);

  mux4to1 mux4to1_1 (.A(Input1), .B(Input2), .C(Input3), .D(Input4), .S1(S1), .S2(S2), .O(O));
endmodule

module mux2to1 (
  input  X,
  input  S,
  input  Y,
  output O
);

  wire and_1_out, and_2_out, not_1_out;

  not not_1 (not_1_out, S);
  and and_1 (and_1_out, X, not_1_out);
  and and_2 (and_2_out, S, Y);
  or or_1 (O, and_1_out, and_2_out);
endmodule

module mux4to1 (
  input  A,
  input  B,
  input  C,
  input  D,
  input  S1,
  input  S2,
  output O
);

  wire mux2to1_1_o, mux2to1_2_o;

  mux2to1 mux2to1_1 (.X(A), .S(S1), .Y(B), .O(mux2to1_1_o));
  mux2to1 mux2to1_2 (.X(C), .S(S1), .Y(D), .O(mux2to1_2_o));
  mux2to1 mux2to1_3 (.X(mux2to1_1_o), .S(S2), .Y(mux2to1_2_o), .O(O));
endmodule
