// Logisim project Lab3.circ as structural Verilog
module full_adder (
  input  A,
  input  Cin,
  input  B,
  output S,
  output Cout
);

  wire and_1_out, and_2_out, xor_1_out;

  and and_1 (and_1_out, A, B);
  xor xor_1 (xor_1_out, A, B);
  xor xor_2 (S, xor_1_out, Cin);
  and and_2 (and_2_out, Cin, xor_1_out);
  or or_1 (Cout, and_2_out, and_1_out);
endmodule

module ripple_carry4 (
  input  [3:0] A,
  input  Cin,
  input  [3:0] B,
  output [3:0] S,
  output Cout
);

  wire full_adder_1_cout, full_adder_2_cout, full_adder_3_cout;

  full_adder full_adder_1 (.A(A[0]), .Cin(Cin), .B(B[0]), .S(S[0]), .Cout(full_adder_1_cout));
  full_adder full_adder_2 (.A(A[1]), .Cin(full_adder_1_cout), .B(B[1]), .S(S[1]), .Cout(full_adder_2_cout));
  full_adder full_adder_3 (.A(A[2]), .Cin(full_adder_2_cout), .B(B[2]), .S(S[2]), .Cout(full_adder_3_cout));
  full_adder full_adder_4 (.A(A[3]), .Cin(full_adder_3_cout), .B(B[3]), .S(S[3]), .Cout(Cout));
endmodule

module op0 (
  input  [3:0] A,
  output [7:0] ALUout
);

  wire [3:0] ripple_carry4_1_s;
  wire [4:4] ripple_carry4_1_cout;

  ripple_carry4 ripple_carry4_1 (.A(A), .Cin(1'b0), .B(4'b0001), .S(ripple_carry4_1_s), .Cout(ripple_carry4_1_cout[4]));
  assign ALUout = {{3{1'b0}}, {ripple_carry4_1_cout[4], ripple_carry4_1_s}};  // Bit_Extender bit_extender_1
endmodule

module op2 (
  input  [3:0] A,
  input  [3:0] B,
  output [7:0] ALUout
);

  wire [6:0] bit_extender_1_out, bit_extender_2_out;

  assign bit_extender_1_out = {{3{1'b0}}, A};  // Bit_Extender bit_extender_1
  assign bit_extender_2_out = {{3{B[3]}}, B};  // Bit_Extender bit_extender_2
  Adder #(.width(7)) adder_1 (
    .a(bit_extender_1_out), .b(bit_extender_2_out), .out({ALUout[7:5], ALUout[3:0]}), .cout(ALUout[4]));  // open: cin
endmodule

module op1 (
  input  [3:0] A,
  input  [3:0] B,
  output [7:0] ALUout
);

  wire [3:0] ripple_carry4_1_s;
  wire [4:4] ripple_carry4_1_cout;

  ripple_carry4 ripple_carry4_1 (.A(A), .Cin(1'b0), .B(B), .S(ripple_carry4_1_s), .Cout(ripple_carry4_1_cout[4]));
  assign ALUout = {{3{1'b0}}, {ripple_carry4_1_cout[4], ripple_carry4_1_s}};  // Bit_Extender bit_extender_1
endmodule

module op3 (
  input  [3:0] A,
  input  [3:0] B,
  output [7:0] ALUout
);

  xor xor_1 (ALUout[0], A[0], B[0]);
  xor xor_2 (ALUout[1], A[1], B[1]);
  xor xor_3 (ALUout[2], A[2], B[2]);
  xor xor_4 (ALUout[3], A[3], B[3]);
  or or_1 (ALUout[4], A[0], B[0]);
  or or_2 (ALUout[5], A[1], B[1]);
  or or_3 (ALUout[6], A[2], B[2]);
  or or_4 (ALUout[7], A[3], B[3]);
endmodule

module op4 (
  input  [3:0] A,
  input  [3:0] B,
  output [7:0] ALUout
);

  wire or_2_out;
  wire [3:0] or_1_out;

  assign or_1_out = A | B;  // OR_Gate or_1, 4 bits wide
  or or_2 (or_2_out, or_1_out[0], or_1_out[1], or_1_out[2], or_1_out[3]);
  assign ALUout = {{7{1'b0}}, or_2_out};  // Bit_Extender bit_extender_1
endmodule

module op5 (
  input  [3:0] A,
  input  [3:0] B,
  output [7:0] ALUout
);


  assign ALUout = {A, B};
endmodule

module ALU (
  input  [3:0] A,
  input  [3:0] B,
  input  [2:0] op,
  output [7:0] ALUout
);

  wire [7:0] op0_1_aluout, op1_1_aluout, op2_1_aluout, op3_1_aluout, op4_1_aluout, op5_1_aluout;

  op1 op1_1 (.A(A), .B(B), .ALUout(op1_1_aluout));
  op3 op3_1 (.A(A), .B(B), .ALUout(op3_1_aluout));
  op4 op4_1 (.A(A), .B(B), .ALUout(op4_1_aluout));
  op5 op5_1 (.A(A), .B(B), .ALUout(op5_1_aluout));
  op2 op2_1 (.A(A), .B(B), .ALUout(op2_1_aluout));
  Multiplexer #(.enable("false"), .select(3), .width(8)) multiplexer_1 (
    .in0(op0_1_aluout), .in1(op2_1_aluout), .in2(op1_1_aluout), .in3(op3_1_aluout), .in4(op4_1_aluout),
    .in5(op5_1_aluout), .out(ALUout), .sel(op));  // open: in6, in7
  op0 op0_1 (.A(A), .ALUout(op0_1_aluout));
endmodule
